# Fritzing sketch Blinking Led (saved by Fritzing 0.9.3b)
breadboards: 1

parts:
  Componente1 = Arduino Uno (Rev3)
  Q1 = Basic FET P-Channel [package="TO220 [THT]"]
  D1 = Rectifier Diode [part_number=1N4001 package="300 mil [THT]"]
  R2 = Resistor [tolerance=±5% resistance=220 package=THT]
  C1 = Electrolytic Capacitor [capacitance=1µF package="100 mil [THT, electrolytic]"]
  M1 = DC Motor

nets:
  N1: Componente1.GND, Q1.source, R2.Pin_0
  N2: Componente1.D3_PWM, Q1.gate, R2.Pin_1
  N3: Componente1.5V, D1.cathode, C1.-, M1.pin_1
  N4: Q1.drain, D1.anode, C1.+, M1.pin_2

custom parts:
  DC Motor: Your standard DC Motor
