# Fritzing sketch Motore Con BOTT (saved by Fritzing 0.9.3b)
breadboards: 1

parts:
  Componente1 = Arduino Uno (Rev3)
  Q1 = Basic FET P-Channel [package="TO220 [THT]"]
  D1 = Rectifier Diode [part_number=1N4001 package="300 mil [THT]"]
  R2 = Resistor [tolerance=±5% resistance=220 package=THT]
  C1 = Electrolytic Capacitor [capacitance=1µF package="100 mil [THT, electrolytic]"]
  S1 = Pushbutton [package="[THT]"]
  M1 = DC Motor

nets:
  N1: Componente1.GND, Q1.source, R2.Pin_0
  N2: Componente1.5V, D1.cathode, C1.-, S1.Pin_3, S1.Pin_4, M1.pin_1
  N3: Q1.gate, R2.Pin_1, S1.Pin_1, S1.Pin_2
  N4: Q1.drain, D1.anode, C1.+, M1.pin_2

custom parts:
  DC Motor: Your standard DC Motor
