# Fritzing sketch Motore Con POT (saved by Fritzing 0.9.3b)
breadboards: 1

parts:
  Componente1 = Arduino Uno (Rev3)
  Q1 = Basic FET P-Channel [package="TO220 [THT]"]
  D1 = Rectifier Diode [part_number=1N4001 package="300 mil [THT]"]
  R2 = Resistor [tolerance=±5% resistance=220 package=THT]
  R3 = Trimmer Potentiometer [maximum_resistance=10kΩ package=THT]
  C1 = Electrolytic Capacitor [capacitance=1µF package="100 mil [THT, electrolytic]"]
  M1 = DC Motor

nets:
  N1: Componente1.GND, Q1.source, R2.Pin_0
  N2: Componente1.5V, D1.cathode, R3.leg1, C1.-, M1.pin_1
  N3: Q1.gate, R2.Pin_1, R3.wiper
  N4: Q1.drain, D1.anode, C1.+, M1.pin_2

custom parts:
  DC Motor: Your standard DC Motor
