# Fritzing sketch Motor_e_Led (saved by Fritzing 0.9.3b)
breadboards: 1

parts:
  Componente1 = Arduino Uno (Rev3)
  LED1 = LED - 5mm [color="Red (633nm)" package="5 mm [THT]"]
  LED2 = LED - 5mm [color="Red (633nm)" package="5 mm [THT]"]
  LED3 = LED - 5mm [color="Red (633nm)" package="5 mm [THT]"]
  LED4 = LED - 5mm [color="Red (633nm)" package="5 mm [THT]"]
  R1 = Resistor [tolerance=±5% resistance=220 package=THT]
  R2 = Resistor [tolerance=±5% resistance=220 package=THT]
  R3 = Resistor [tolerance=±5% resistance=220 package=THT]
  R4 = Resistor [tolerance=±5% resistance=220 package=THT]
  Q1 = Basic FET P-Channel [package="TO220 [THT]"]
  R5 = Resistor [tolerance=±5% resistance=220 package=THT]
  D1 = Rectifier Diode [part_number=1N4001 package="300 mil [THT]"]
  C1 = Electrolytic Capacitor [capacitance=1µF package="100 mil [THT, electrolytic]"]
  M1 = DC Motor

nets:
  N1: Componente1.GND, Q1.source, R5.Pin_0
  N2: Componente1.D3_PWM, Q1.gate, R5.Pin_1
  N3: Componente1.D4, R1.Pin_1
  N4: Componente1.D5_PWM, R2.Pin_1
  N5: Componente1.D6_PWM, R3.Pin_1
  N6: Componente1.D7, R4.Pin_1
  N7: Componente1.5V, LED1.cathode, LED2.cathode, LED3.cathode, LED4.cathode, D1.cathode, C1.-, M1.pin_1
  N8: LED1.anode, R4.Pin_0
  N9: LED2.anode, R3.Pin_0
  N10: LED3.anode, R2.Pin_0
  N11: LED4.anode, R1.Pin_0
  N12: Q1.drain, D1.anode, C1.+, M1.pin_2

custom parts:
  DC Motor: Your standard DC Motor
